// Digital circuit 16x4bitMEMV3.dig as structural Verilog
module _16x4bitMEMV3 (
  input  [3:0] A,
  input  [3:0] D_in,
  input  [1:0] In,
  input  CLK,
  output [3:0] D_out
);

  wire [1:0] demultiplexer_1_out_0, demultiplexer_1_out_1, demultiplexer_1_out_2, demultiplexer_1_out_3,
       demultiplexer_1_out_4, demultiplexer_1_out_5, demultiplexer_1_out_6, demultiplexer_1_out_7,
       demultiplexer_1_out_8, demultiplexer_1_out_9, demultiplexer_1_out_10, demultiplexer_1_out_11,
       demultiplexer_1_out_12, demultiplexer_1_out_13, demultiplexer_1_out_14, demultiplexer_1_out_15;
  wire [3:0] memcell_1_q, memcell_2_q, memcell_3_q, memcell_4_q, memcell_5_q, memcell_6_q, memcell_7_q,
       memcell_8_q, memcell_9_q, memcell_10_q, memcell_11_q, memcell_12_q, memcell_13_q, memcell_14_q,
       memcell_15_q, memcell_16_q;

  Demultiplexer #(.Selector_Bits(4), .Bits(2)) demultiplexer_1 (
    .sel(A), .in(In), .out_0(demultiplexer_1_out_0), .out_1(demultiplexer_1_out_1),
    .out_2(demultiplexer_1_out_2), .out_3(demultiplexer_1_out_3), .out_4(demultiplexer_1_out_4),
    .out_5(demultiplexer_1_out_5), .out_6(demultiplexer_1_out_6), .out_7(demultiplexer_1_out_7),
    .out_8(demultiplexer_1_out_8), .out_9(demultiplexer_1_out_9), .out_10(demultiplexer_1_out_10),
    .out_11(demultiplexer_1_out_11), .out_12(demultiplexer_1_out_12), .out_13(demultiplexer_1_out_13),
    .out_14(demultiplexer_1_out_14), .out_15(demultiplexer_1_out_15));
  MemCell memcell_1 (.Ctrl(demultiplexer_1_out_0), .In(D_in), .Clk(CLK), .Q(memcell_1_q));
  MemCell memcell_2 (.Ctrl(demultiplexer_1_out_1), .In(D_in), .Clk(CLK), .Q(memcell_2_q));
  MemCell memcell_3 (.Ctrl(demultiplexer_1_out_2), .In(D_in), .Clk(CLK), .Q(memcell_3_q));
  MemCell memcell_4 (.Ctrl(demultiplexer_1_out_3), .In(D_in), .Clk(CLK), .Q(memcell_4_q));
  MemCell memcell_5 (.Ctrl(demultiplexer_1_out_4), .In(D_in), .Clk(CLK), .Q(memcell_5_q));
  MemCell memcell_6 (.Ctrl(demultiplexer_1_out_5), .In(D_in), .Clk(CLK), .Q(memcell_6_q));
  MemCell memcell_7 (.Ctrl(demultiplexer_1_out_6), .In(D_in), .Clk(CLK), .Q(memcell_7_q));
  MemCell memcell_8 (.Ctrl(demultiplexer_1_out_7), .In(D_in), .Clk(CLK), .Q(memcell_8_q));
  MemCell memcell_9 (.Ctrl(demultiplexer_1_out_8), .In(D_in), .Clk(CLK), .Q(memcell_9_q));
  MemCell memcell_10 (.Ctrl(demultiplexer_1_out_9), .In(D_in), .Clk(CLK), .Q(memcell_10_q));
  MemCell memcell_11 (.Ctrl(demultiplexer_1_out_10), .In(D_in), .Clk(CLK), .Q(memcell_11_q));
  MemCell memcell_12 (.Ctrl(demultiplexer_1_out_11), .In(D_in), .Clk(CLK), .Q(memcell_12_q));
  MemCell memcell_13 (.Ctrl(demultiplexer_1_out_12), .In(D_in), .Clk(CLK), .Q(memcell_13_q));
  MemCell memcell_14 (.Ctrl(demultiplexer_1_out_13), .In(D_in), .Clk(CLK), .Q(memcell_14_q));
  MemCell memcell_15 (.Ctrl(demultiplexer_1_out_14), .In(D_in), .Clk(CLK), .Q(memcell_15_q));
  MemCell memcell_16 (.Ctrl(demultiplexer_1_out_15), .In(D_in), .Clk(CLK), .Q(memcell_16_q));
  Multiplexer #(.Selector_Bits(4), .Bits(4)) multiplexer_1 (
    .sel(A), .in_0(memcell_1_q), .in_1(memcell_2_q), .in_2(memcell_3_q), .in_3(memcell_4_q),
    .in_4(memcell_5_q), .in_5(memcell_6_q), .in_6(memcell_7_q), .in_7(memcell_8_q), .in_8(memcell_9_q),
    .in_9(memcell_10_q), .in_10(memcell_11_q), .in_11(memcell_12_q), .in_12(memcell_13_q),
    .in_13(memcell_14_q), .in_14(memcell_15_q), .in_15(memcell_16_q), .out(D_out));
endmodule
