// Digital circuit 4 bit adder.dig as structural Verilog
module _4_bit_adder (
  input  [3:0] A,
  input  [3:0] B,
  output [3:0] Sum,
  output C_out
);

  wire adder_1_cout, adder_2_cout, adder_3_cout;

  Adder adder_1 (.a(A[0]), .b(B[0]), .cin(1'b0), .Sum(Sum[0]), .cout(adder_1_cout));
  Adder adder_2 (.a(A[1]), .b(B[1]), .cin(adder_1_cout), .Sum(Sum[1]), .cout(adder_2_cout));
  Adder adder_3 (.a(A[2]), .b(B[2]), .cin(adder_2_cout), .Sum(Sum[2]), .cout(adder_3_cout));
  Adder adder_4 (.a(A[3]), .b(B[3]), .cin(adder_3_cout), .Sum(Sum[3]), .cout(C_out));
endmodule
