// Digital circuit 4 bit subtractor.dig as structural Verilog
module _4_bit_subtractor (
  input  [3:0] A,
  input  [3:0] B,
  output [3:0] Sum
);

  wire adder_1_cout, adder_2_cout, adder_3_cout, xor_1_out, xor_2_out, xor_3_out, xor_4_out;

  xor xor_1 (xor_1_out, B[0], 1'b1);
  xor xor_2 (xor_2_out, B[1], 1'b1);
  xor xor_3 (xor_3_out, B[2], 1'b1);
  xor xor_4 (xor_4_out, B[3], 1'b1);
  Adder adder_1 (.a(A[0]), .b(xor_1_out), .cin(1'b1), .Sum(Sum[0]), .cout(adder_1_cout));
  Adder adder_2 (.a(A[1]), .b(xor_2_out), .cin(adder_1_cout), .Sum(Sum[1]), .cout(adder_2_cout));
  Adder adder_3 (.a(A[2]), .b(xor_3_out), .cin(adder_2_cout), .Sum(Sum[2]), .cout(adder_3_cout));
  Adder adder_4 (.a(A[3]), .b(xor_4_out), .cin(adder_3_cout), .Sum(Sum[3]));  // open: cout
endmodule
