// Digital circuit 4 bit zero flag.dig as structural Verilog
module _4_bit_zero_flag (
  input  [3:0] In,
  output Out
);

  nor nor_1 (Out, In[0], In[1], In[2], In[3]);
  LED led_1 (.in(Out));
endmodule
