// Digital circuit 4bi_ALU.dlogic.dig as structural Verilog
module _4bi_ALU_dlogic (
  input  [3:0] A,
  input  [3:0] B,
  input  [2:0] CTR,
  output Overflow,
  output _0_FLAG,
  output SLT,
  output [3:0] OPP
);

  wire [3:0] _4_bit_adder_1_sum, _4_bit_or_1_or, _4_bit_subtractor_1_sum, _4bit_and_1_and, _4bit_xor_1_xor;

  _4bit_XOR _4bit_xor_1 (.a(A), .b(B), .XOR(_4bit_xor_1_xor));
  _4_bit_OR _4_bit_or_1 (.a(A), .b(B), .OR(_4_bit_or_1_or));
  _4bit_AND _4bit_and_1 (.a(A), .b(B), .AND(_4bit_and_1_and));
  _4_bit_adder _4_bit_adder_1 (.A(A), .B(B), .Sum(_4_bit_adder_1_sum), .C_out(Overflow));
  _4_bit_subtractor _4_bit_subtractor_1 (.A(A), .B(B), .Sum(_4_bit_subtractor_1_sum));
  SLT slt_1 (.A(A), .B(B), .Logic_output(SLT));
  Multiplexer #(.Selector_Bits(3), .Bits(4)) multiplexer_1 (
    .sel(CTR), .in_0(_4_bit_adder_1_sum), .in_1(_4_bit_subtractor_1_sum), .in_2(_4bit_and_1_and),
    .in_3(_4_bit_or_1_or), .in_4(_4bit_xor_1_xor), .in_5(4'b0000), .in_6(4'b0000), .in_7(4'b0000), .out(OPP));
  _4_bit_zero_flag _4_bit_zero_flag_1 (.In(_4_bit_adder_1_sum), .Out(_0_FLAG));

  // Notes on the sheet:
  //   Overflow: Carry out from the Adder function
endmodule
