// Digital circuit 4bit_AND.dig as structural Verilog
module _4bit_AND (
  input  [3:0] a,
  input  [3:0] b,
  output [3:0] AND
);

  and and_1 (AND[0], a[0], b[0]);
  and and_2 (AND[1], a[1], b[1]);
  and and_3 (AND[2], a[2], b[2]);
  and and_4 (AND[3], a[3], b[3]);
endmodule
