// Digital circuit 4bit_PC.dig as structural Verilog
module _4bit_PC (
  input  Clock,
  input  Sel,
  input  [1:0] Control,
  input  [3:0] Load,
  output [3:0] Q_plus_1
);

  wire [3:0] INC_p2, multiplexer_1_out;

  Multiplexer #(.Bits(4)) multiplexer_1 (.sel(Sel), .in_0(INC_p2), .in_1(Load), .out(multiplexer_1_out));
  _4bit_RegisterV2 _4bit_registerv2_1 (.Clock(Clock), .D(multiplexer_1_out), .Control(Control), .Q(Q_plus_1));
  // _4bit_Incrementor INC: pin names not known; wires that end beside it: Q_plus_1, INC_p2

  // Notes on the sheet:
  //   Sel: Pick between incrementing the current instruction or jumping to another
  //   Load: Jumps to whatever instruction is inputted
endmodule
