// Digital circuit 4bit_Processor.dig as structural Verilog
module _4bit_Processor (
  input  [3:0] RAM_data,
  input  RAM_Read,
  input  RAM_Write,
  input  [3:0] PC_load,
  input  [1:0] PC_ctrl,
  input  PC_selector,
  input  clk,
  input  CU_enable,
  output [3:0] ALUOut,
  output ZeroFlag,
  output [3:0] Address
);

  wire CU_if, CU_il, CU_rr1, CU_rr2, CU_wr;
  wire [0:0] fde_cycle_1_f;
  wire [1:0] CU_we;
  wire [2:0] CU_alu;
  wire [3:0] IR_q, multiplexer_1_out, RAM_d_out, Register_File_rd1, Register_File_rd2;

  _4bit_PC PC (.Clock(clk), .Sel(PC_selector), .Control(PC_ctrl), .Load(PC_load), .Q_plus_1(Address));
  FDE_Cycle fde_cycle_1 (.CLK(clk), .IN(CU_if), .F(fde_cycle_1_f[0]));  // open: D, E
  RAMV1 RAM (.A(Address), .D_in(RAM_data), .Read(RAM_Read), .Write(RAM_Write), .CLK(clk), .D_out(RAM_d_out));
  _4bit_RegisterV2 IR (.Clock(clk), .D(RAM_d_out), .Control({1'b0, fde_cycle_1_f[0]}), .Q(IR_q));
  Control_Unit CU (
    .A(IR_q[3]), .B(IR_q[2]), .C(IR_q[1]), .D(IR_q[0]), .Clk(clk), .Enable(CU_enable), .RR1(CU_rr1),
    .RR2(CU_rr2), .WR(CU_wr), .WE(CU_we), .IL(CU_il), .ALU(CU_alu), .IF(CU_if));
  Multiplexer #(.Bits(4)) multiplexer_1 (.sel(CU_il), .in_0(RAM_d_out), .in_1(ALUOut), .out(multiplexer_1_out));
  yahyasregFileV2 Register_File (
    .RR1(CU_rr1), .WR(CU_wr), .Data_in(multiplexer_1_out), .Clk(clk), .Cnr(CU_we), .RR2(CU_rr2),
    .RD1(Register_File_rd1), .RD2(Register_File_rd2));
  _4bi_ALU_dlogic ALU (
    .A(Register_File_rd1), .B(Register_File_rd2), .CTR(CU_alu), ._0_FLAG(ZeroFlag), .OPP(ALUOut));  // open: Overflow, SLT
endmodule
