// Digital circuit 4bit_RegisterV2.dig as structural Verilog
module _4bit_RegisterV2 (
  input  Clock,
  input  [3:0] D,
  input  [1:0] Control,
  output [3:0] Q
);

  wire [3:0] multiplexer_1_out;

  Multiplexer #(.Selector_Bits(2), .Bits(4)) multiplexer_1 (
    .sel(Control), .in_0(Q), .in_1(D), .in_2(4'b0000), .in_3(4'b0000), .out(multiplexer_1_out));
  D_FF D0 (.D(multiplexer_1_out[0]), .C(Clock), .Q(Q[0]));  // open: nQ
  D_FF d_ff_1 (.D(multiplexer_1_out[1]), .C(Clock), .Q(Q[1]));  // open: nQ
  D_FF d_ff_2 (.D(multiplexer_1_out[2]), .C(Clock), .Q(Q[2]));  // open: nQ
  D_FF d_ff_3 (.D(multiplexer_1_out[3]), .C(Clock), .Q(Q[3]));  // open: nQ
endmodule
