// Digital circuit 4bit_XOR.dig as structural Verilog
module _4bit_XOR (
  input  [3:0] a,
  input  [3:0] b,
  output [3:0] XOR
);

  xor xor_1 (XOR[0], a[0], b[0]);
  xor xor_2 (XOR[1], a[1], b[1]);
  xor xor_3 (XOR[2], a[2], b[2]);
  xor xor_4 (XOR[3], a[3], b[3]);
endmodule
