// Digital circuit 4bit_memoryV2.dig as structural Verilog
module _4bit_memoryV2 (
  input  [3:0] D_in,
  input  Write,
  output [3:0] D_out
);

  D_FF d_ff_1 (.D(D_in[0]), .C(Write), .Q(D_out[0]));  // open: nQ
  D_FF d_ff_2 (.D(D_in[1]), .C(Write), .Q(D_out[1]));  // open: nQ
  D_FF d_ff_3 (.D(D_in[2]), .C(Write), .Q(D_out[2]));  // open: nQ
  D_FF d_ff_4 (.D(D_in[3]), .C(Write), .Q(D_out[3]));  // open: nQ
endmodule
