// Digital circuit Adder.dig as structural Verilog
module Adder (
  input  a,
  input  b,
  input  cin,
  output Sum,
  output cout
);

  wire and_1_out, and_2_out, xor_1_out;

  and and_1 (and_1_out, b, a);
  xor xor_1 (xor_1_out, a, b);
  or or_1 (cout, and_2_out, and_1_out);
  and and_2 (and_2_out, xor_1_out, cin);
  xor xor_2 (Sum, cin, xor_1_out);
endmodule
