// Digital circuit Control_Unit.dig as structural Verilog
module Control_Unit (
  input  A,
  input  B,
  input  C,
  input  D,
  input  Clk,
  input  Enable,
  output RR1,
  output RR2,
  output WR,
  output [1:0] WE,
  output IL,
  output [2:0] ALU,
  output IF
);

  wire and_1_out, and_2_out, AND_3_p5, and_4_out, and_5_out, LSB_q, MSB_q, not_1_out, not_2_out, not_3_out,
       not_4_out, or_1_out, OR_2_p5, or_3_out, SLT_p5, SUB_p5, XOR_p5;

  not not_1 (not_1_out, Enable);
  and and_1 (and_1_out, MSB_q, not_1_out);
  and and_2 (and_2_out, Enable, LSB_q);
  or or_1 (or_1_out, and_1_out, and_2_out);
  // RR1 RR1: pin names not known; wires that end beside it: A, RR1
  // RR2 RR2: pin names not known; wires that end beside it: RR2
  // WR WR: pin names not known; wires that end beside it: A, B, C, D, WR
  // WE WE: pin names not known; wires that end beside it: A, C, D, WE[0]
  // ADD_Sel ADD: pin names not known; wires that end beside it: A, B, C, D
  // SUB_Sel SUB: pin names not known; wires that end beside it: A, B, C, D, SUB_p5
  // AND_Sel AND_3: pin names not known; wires that end beside it: A, B, C, D, AND_3_p5
  // OR_Sel OR_2: pin names not known; wires that end beside it: A, B, C, D, OR_2_p5
  // XOR_Sel XOR: pin names not known; wires that end beside it: A, B, C, D, XOR_p5
  // SLT_Sel SLT: pin names not known; wires that end beside it: A, B, C, D, SLT_p5
  // IL IL: pin names not known; wires that end beside it: A, C, D, IL
  not not_2 (not_2_out, Enable);
  not not_3 (not_3_out, MSB_q);
  not not_4 (not_4_out, LSB_q);
  and and_4 (and_4_out, not_2_out, LSB_q);
  and and_5 (and_5_out, not_3_out, not_4_out, Enable);
  or or_3 (or_3_out, and_4_out, and_5_out);
  D_FF MSB (.D(or_1_out), .C(Clk), .Q(MSB_q));  // open: nQ
  or or_4 (ALU[0], SUB_p5, OR_2_p5, SLT_p5);
  D_FF LSB (.D(or_3_out), .C(Clk), .Q(LSB_q));  // open: nQ
  nor nor_1 (IF, MSB_q, LSB_q);
  or or_5 (ALU[1], AND_3_p5, OR_2_p5);
  or or_6 (ALU[2], XOR_p5, SLT_p5);

  assign WE[1] = 1'b0;

  // Notes on the sheet:
  //   ALU: Opereation Selector
endmodule
