// Digital circuit MemCell.dig as structural Verilog
module MemCell (
  input  [1:0] Ctrl,
  input  [3:0] In,
  input  Clk,
  output [3:0] Q
);

  wire [3:0] multiplexer_1_out;

  _4bit_memoryV2 _4bit_memoryv2_1 (.D_in(multiplexer_1_out), .Write(Clk), .D_out(Q));
  Multiplexer #(.Selector_Bits(2), .Bits(4)) multiplexer_1 (
    .sel(Ctrl), .in_0(Q), .in_1(In), .in_2(4'b0000), .in_3(4'b0000), .out(multiplexer_1_out));
endmodule
