// Digital circuit RAMV1.dig as structural Verilog
module RAMV1 (
  input  [3:0] A,
  input  [3:0] D_in,
  input  Read,
  input  Write,
  input  CLK,
  output [3:0] D_out
);

  wire and_1_out, xor_1_out;
  wire [0:0] and_2_out;
  wire [3:0] _16x4bitmemv3_1_d_out;

  xor xor_1 (xor_1_out, Read, Write);
  and and_1 (and_1_out, Read, xor_1_out);
  and and_2 (and_2_out[0], xor_1_out, Write);
  _16x4bitMEMV3 _16x4bitmemv3_1 (
    .A(A), .D_in(D_in), .In({1'b0, and_2_out[0]}), .CLK(CLK), .D_out(_16x4bitmemv3_1_d_out));
  assign D_out = and_1_out ? _16x4bitmemv3_1_d_out : 4'bz;  // Driver driver_1
endmodule
