// Digital circuit SLT.dig as structural Verilog
module SLT (
  input  [3:0] A,
  input  [3:0] B,
  output Logic_output
);

  wire [2:0] _4_bit_subtractor__1_1_p3;

  // _4_bit_subtractor__1 _4_bit_subtractor__1_1: pin names not known; wires that end beside it: A, B, {Logic_output, _4_bit_subtractor__1_1_p3}
endmodule
