// Digital circuit yahyasregFileV2.dig as structural Verilog
module yahyasregFileV2 (
  input  RR1,
  input  WR,
  input  [3:0] Data_in,
  input  Clk,
  input  [1:0] Cnr,
  input  RR2,
  output [3:0] RD1,
  output [3:0] RD2
);

  wire [3:0] _4bit_registerv2_1_q, _4bit_registerv2_2_q, demultiplexer_1_out_0, demultiplexer_1_out_1;

  Demultiplexer #(.Bits(4)) demultiplexer_1 (
    .sel(WR), .in(Data_in), .out_0(demultiplexer_1_out_0), .out_1(demultiplexer_1_out_1));
  _4bit_RegisterV2 _4bit_registerv2_1 (.Clock(Clk), .D(demultiplexer_1_out_0), .Control(Cnr), .Q(_4bit_registerv2_1_q));
  _4bit_RegisterV2 _4bit_registerv2_2 (.Clock(Clk), .D(demultiplexer_1_out_1), .Control(Cnr), .Q(_4bit_registerv2_2_q));
  Multiplexer #(.Bits(4)) multiplexer_1 (
    .sel(RR1), .in_0(_4bit_registerv2_1_q), .in_1(_4bit_registerv2_2_q), .out(RD1));
  Multiplexer #(.Bits(4)) multiplexer_2 (
    .sel(RR2), .in_0(_4bit_registerv2_1_q), .in_1(_4bit_registerv2_2_q), .out(RD2));
endmodule
